# Fritzing sketch panic_button (saved by Fritzing 0.9.3b)
breadboards: 1

parts:
  Teensy1 = Teensy 2.0
  LED1 = RGB LED - (4 legs) [package="5 mm [THT]"]
  R1 = Resistor [tolerance=±5% resistance=220 package="0805 [SMD]"]
  R2 = Resistor [tolerance=±5% resistance=220 package="0805 [SMD]"]
  R3 = Resistor [tolerance=±5% resistance=220 package="0805 [SMD]"]
  BUTTON1 = Arcade Button (red)
  R4 = Resistor [tolerance=±5% resistance=220 package="0805 [SMD]"]

nets:
  N1: Teensy1.GND, LED1.common_anode, BUTTON1.no_name_yet#1
  N2: Teensy1.D2, BUTTON1.no_name_yet#2, R4.Pin_1
  N3: Teensy1.D7, R1.Pin_1
  N4: Teensy1.B5, R2.Pin_1
  N5: Teensy1.B6, R3.Pin_0
  N6: Teensy1.VCC, R4.Pin_0
  N7: LED1.red_cathode, R3.Pin_1
  N8: LED1.green_cathode, R2.Pin_0
  N9: LED1.blue_cathode, R1.Pin_0

custom parts:
  Arcade Button (red): Adafruit Arcade Button (red)
